// Logisim project RISC 32 BIT ALU.circ as structural Verilog: 1 circuit, main circuit main
module main (
  input  [2:0] in_1,
  input  [2:0] OpeartionCode,
  input  [31:0] OP1,
  input  [31:0] OP2,
  input  Clock,
  output [31:0] Result
);

  wire Arithmetic, Logic, subtractor_1_bout;
  wire [31:0] adder_1_out, adder_2_out, and_1_out, divider_1_out, divider_2_rem, multiplexer_1_out,
       multiplexer_2_out, multiplexer_3_out, multiplier_1_out, or_1_out, shifter_1_out, shifter_2_out,
       subtractor_1_out, subtractor_2_out, xor_1_out;

  Adder #(.width(32)) adder_1 (.a(OP1), .b(OP2), .out(adder_1_out));  // open: cin, cout
  Subtractor #(.width(32)) subtractor_1 (
    .a(OP1), .b(OP2), .out(subtractor_1_out), .bin(1'b0), .bout(subtractor_1_bout));
  Multiplier #(.width(32)) multiplier_1 (.a(OP1), .b(OP2), .out(multiplier_1_out));  // open: cin, cout
  Divider #(.width(32)) divider_1 (.a(OP1), .out(divider_1_out));  // open: b, upper, rem
  Divider #(.width(32)) divider_2 (.a(OP1), .b(OP2), .rem(divider_2_rem));  // open: out, upper
  Adder #(.width(32)) adder_2 (.a(OP1), .b(32'h1), .out(adder_2_out));  // open: cin, cout
  Subtractor #(.width(32)) subtractor_2 (.a(OP1), .b(32'h1), .out(subtractor_2_out));  // open: bin, bout
  assign and_1_out = OP1 & OP2;  // AND_Gate and_1, 32 bits wide
  assign or_1_out = OP1 | OP2;  // OR_Gate or_1, 32 bits wide
  assign xor_1_out = OP1 ^ OP2;  // XOR_Gate xor_1, 32 bits wide
  Shifter #(.width(32)) shifter_1 (.in(OP1), .\dist (OP2[4:0]), .out(shifter_1_out));
  Shifter #(.width(32), .shift("lr")) shifter_2 (.in(OP1), .\dist (OP2[4:0]), .out(shifter_2_out));
  Multiplexer #(.select(3), .width(32)) multiplexer_1 (
    .in1(and_1_out), .in2(or_1_out), .in3(xor_1_out), .in5(shifter_1_out), .in6(shifter_2_out),
    .out(multiplexer_1_out), .sel(OpeartionCode), .en(Logic));  // open: in0, in4, in7
  Multiplexer #(.select(3), .width(32)) multiplexer_2 (
    .in0(adder_1_out), .in1(subtractor_1_out), .in2(multiplier_1_out), .in3(divider_1_out),
    .in4(divider_2_rem), .in5(adder_2_out), .in6(subtractor_2_out), .out(multiplexer_2_out),
    .sel(OpeartionCode), .en(Arithmetic));  // open: in7
  // Probe on multiplexer_2_out
  // Probe on multiplexer_1_out
  and and_2 (Logic, ~in_1[2], ~in_1[1], ~in_1[0]);  // AND_Gate
  Multiplexer #(.width(32)) multiplexer_3 (
    .in0(multiplexer_2_out), .in1(multiplexer_1_out), .out(multiplexer_3_out), .sel(Logic), .en(1'b1));
  and and_3 (Arithmetic, ~in_1[2], ~in_1[1], in_1[0]);  // AND_Gate
  // Probe on Result
  Register #(.width(32)) register_1 (.D(multiplexer_3_out), .en(1'b1), .Q(Result), .clk(Clock));  // open: clr

  // Other names for the same wires on the sheet: OP29 = in_1[0]; OP30 = in_1[1]; OP31 = in_1[2];
  //   Shift[4:0] = OP2[4:0]; OPCODE[2:0] = OpeartionCode
endmodule
