// Logisim project RISC 32 BIT DECODE.circ as structural Verilog: 1 circuit, main circuit main
module main (
  input  [31:0] Instruction,
  input  Clock,
  output out_3,
  output out_4,
  output out_5,
  output out_6,
  output out_7,
  output out_8,
  output out_9,
  output out_10,
  output out_11,
  output out_12,
  output out_13,
  output out_14,
  output out_15,
  output out_16,
  output out_17,
  output out_18,
  output out_19,
  output out_20,
  output out_21,
  output out_22,
  output out_23,
  output out_24,
  output Arithmetic,
  output Logic,
  output BranchJump,
  output RegInstr,
  output Stack,
  output out_30,
  output out_31,
  output out_32,
  output out_33,
  output out_34,
  output out_35,
  output out_36,
  output [7:0] out_37,
  output [7:0] out_38,
  output [7:0] out_39,
  output [1:0] out_40
);

  wire [7:2] Fourth;

  and and_1 (Arithmetic, ~Fourth[7], ~Fourth[6], Fourth[5]);  // AND_Gate
  and and_2 (Logic, ~Fourth[7], ~Fourth[6], ~Fourth[5]);  // AND_Gate
  and and_3 (BranchJump, ~Fourth[7], Fourth[6]);  // AND_Gate
  Register #(.width(32)) Instruction_Register (
    .D(Instruction), .en(1'b1), .Q({Fourth, out_40, out_37, out_38, out_39}), .clk(Clock), .clr(1'b0));
  and and_4 (RegInstr, Fourth[7], Fourth[6], ~Fourth[5]);  // AND_Gate
  and and_5 (Stack, Fourth[7], ~Fourth[6], ~Fourth[5]);  // AND_Gate
  Decoder #(.select(3)) decoder_1 (
    .out1(out_10), .out2(out_11), .out3(out_12), .out4(out_13), .out5(out_14), .out6(out_15),
    .sel(Fourth[4:2]), .en(Logic));  // open: out0, out7
  Decoder decoder_2 (.out0(out_16), .out1(out_17), .sel(Fourth[2]), .en(Stack));
  Decoder #(.select(3)) decoder_3 (
    .out0(out_18), .out1(out_19), .out2(out_20), .out3(out_21), .out4(out_22), .out5(out_23), .out6(out_24),
    .out7(out_30), .sel(Fourth[4:2]), .en(BranchJump));
  Decoder #(.select(3)) decoder_4 (
    .out0(out_32), .out1(out_33), .out2(out_34), .out3(out_35), .sel(Fourth[4:2]), .en(RegInstr));  // open: out4, out5, out6, out7
  Decoder #(.select(3)) decoder_5 (
    .out0(out_3), .out1(out_4), .out2(out_5), .out3(out_6), .out4(out_7), .out5(out_8), .out6(out_9),
    .sel(Fourth[4:2]), .en(Arithmetic));  // open: out7
  and and_6 (out_36, Fourth[5], Fourth[6], Fourth[7], Fourth[2], Fourth[3], Fourth[4]);
  and and_7 (out_31, BranchJump, Fourth[5], ~Fourth[2], ~Fourth[3], ~Fourth[4]);  // AND_Gate

  // Other names for the same wires on the sheet: First[7:0] = out_39; OP2[7:0] = out_39; OP1[7:0] = out_38;
  //   Second[7:0] = out_38; Dest[7:0] = out_37; Third[7:0] = out_37; Fourth[1:0] = out_40; Number[1:0] = out_40;
  //   Instruction_t[2:0] = Fourth[4:2]; IR29 = Fourth[5]; Type[2:0] = Fourth[7:5]; IR30 = Fourth[6]; IR31 = Fourth[7];
  //   ADD = out_3; AND = out_10; BEQ = out_20; BGE = out_22; BGT = out_21; BLEQ = out_23; BLSS = out_19;
  //   BNEQ = out_24; CLR = out_35; CMP = out_13; DEC = out_9; DIV = out_6; HALT = out_36; INC = out_8; JSR = out_30;
  //   JUMP = out_18; LD = out_32; LSH = out_14; MOD = out_7; MOV = out_34; MUL = out_5; OR = out_11; POP = out_16;
  //   PUSH = out_17; RSH = out_15; RTS = out_31; ST = out_33; SUB = out_4; XOR = out_12
endmodule
