// Logisim project RISC 32 BIT MAIN.circ as structural Verilog: 1 circuit, main circuit main
module main (
  input  [31:0] in_1
);

  wire and_2_out, and_3_out, and_5_out, Arithmetic, Clock, clock_1_out, CLR, controlled_buffer_3_out, EnOP1,
       EnOP2, EnRC, HALT, LD, Logic, MOV, multiplexer_4_out, not_1_out, not_2_out, not_3_out, not_4_out,
       OneAddress, or_1_out, or_2_out, or_3_out, or_4_out, or_6_out, or_7_out, ThreeAddress, TwoAddress,
       ZeroAddress;
  wire [1:0] Num, SelectInput, SelectREG;
  wire [2:0] Instr, OPCODE;
  wire [4:0] REG1, REG2;
  wire [7:0] Dest;
  wire [15:0] Input;
  wire [31:0] Accumulator, controlled_buffer_1_out, controlled_buffer_2_out, main_1_result,
       multiplexer_1_out, multiplexer_2_out, multiplexer_3_out, OP1, OP2, Result;

  Clock clock_1 (.out(clock_1_out));
  Multiplexer #(.width(32)) multiplexer_1 (
    .in0(OP1), .in1(Accumulator), .out(multiplexer_1_out), .sel(OneAddress), .en(1'b1));
  Multiplexer #(.width(32)) multiplexer_2 (.in0(OP2), .in1(OP1), .out(multiplexer_2_out), .sel(OneAddress), .en(1'b1));
  and and_1 (Clock, clock_1_out, ~HALT);  // AND_Gate
  assign controlled_buffer_1_out = OneAddress ? Result : 32'bz;  // Controlled_Buffer controlled_buffer_1
  RISC_32_BIT_ALU_main main_1 (
    .Clock(Clock), .Result(main_1_result), .OP1(multiplexer_1_out), .OP2(multiplexer_2_out),
    .OpeartionCode(OPCODE), .in_1(Instr));
  Register #(.width(32)) u_Accumulator (
    .D(controlled_buffer_1_out), .en(OneAddress), .Q(Accumulator), .clk(Clock), .clr(and_2_out));
  and and_2 (and_2_out, ZeroAddress, CLR);
  // RISC_32_BIT_DECODE_main main_2: pin names not known; wires that end beside it: in_1, Clock, OPCODE, Instr, LD, MOV, CLR, HALT, Dest, Input[15:8], Input[7:0], Num, Arithmetic, Logic
  // Probe on main_1_result
  and and_3 (and_3_out, or_1_out, not_1_out);
  or or_1 (or_1_out, Logic, Arithmetic);
  RISC_32_BIT_MEMORY_main main_3 (.in_3(Clock));  // open: in_1, in_2, in_4, in_5, in_6, out_7, out_8
  Register #(.width(32)) register_1 (.D(main_1_result), .en(and_3_out), .Q(Result), .clk(Clock), .clr(1'b0));
  not not_1 (not_1_out, MOV);
  not not_2 (not_2_out, MOV);
  assign controlled_buffer_2_out = not_2_out ? Result : 32'bz;  // Controlled_Buffer controlled_buffer_2
  not not_3 (not_3_out, OneAddress);
  Multiplexer #(.select(2), .width(32)) multiplexer_3 (
    .in0(controlled_buffer_2_out), .in1(OP1), .in2({{16{1'b0}}, Input}), .out(multiplexer_3_out),
    .sel(SelectInput), .en(not_3_out));  // open: in3
  Multiplexer multiplexer_4 (.in0(1'b0), .in1(1'b1), .out(multiplexer_4_out), .sel(CLR), .en(1'b1));
  assign controlled_buffer_3_out = not_4_out ? EnOP1 : 1'bz;  // Controlled_Buffer controlled_buffer_3
  not not_4 (not_4_out, MOV);
  Pull_Resistor pull_resistor_1 (.node(EnRC));
  Pull_Resistor pull_resistor_2 (.node(controlled_buffer_3_out));
  Pull_Resistor pull_resistor_3 (.node(EnOP2));
  // RISC_32_BIT_REGISTERS_main main_4: pin names not known; wires that end beside it: multiplexer_3_out, Dest[4:0], REG1, REG2, EnRC, multiplexer_4_out, controlled_buffer_3_out, EnOP2, Clock, OP1, OP2
  Multiplexer #(.select(2), .width(5)) multiplexer_5 (
    .in1(Dest[4:0]), .in2(Dest[4:0]), .in3(Input[12:8]), .out(REG1), .sel(SelectREG), .en(1'b1));  // open: in0
  Multiplexer #(.select(2), .width(5)) multiplexer_6 (
    .in0({5{1'b0}}), .in1({5{1'b0}}), .in2(Input[12:8]), .in3(Input[4:0]), .out(REG2), .sel(SelectREG),
    .en(1'b1));
  or or_2 (or_2_out, ThreeAddress, TwoAddress, OneAddress);
  or or_3 (or_3_out, ThreeAddress, TwoAddress);
  or or_4 (or_4_out, or_2_out, MOV);
  and and_4 (EnOP2, or_3_out, ~ZeroAddress, ~MOV, ~LD);  // AND_Gate
  or or_5 (EnRC, Arithmetic, Logic, MOV, LD);
  and and_5 (and_5_out, TwoAddress, ~MOV);  // AND_Gate
  and and_6 (EnOP1, or_4_out, ~ZeroAddress, ~LD, ~CLR);  // AND_Gate
  Priority_Encoder #(.select(2)) priority_encoder_1 (
    .in1(OneAddress), .in2(and_5_out), .in3(or_6_out), .out(SelectREG));  // open: in0, gs, en_out, en_in
  or or_6 (or_6_out, ThreeAddress, MOV);
  or or_7 (or_7_out, Arithmetic, Logic);
  Priority_Encoder #(.select(2)) priority_encoder_2 (
    .in0(or_7_out), .in1(MOV), .in2(LD), .out(SelectInput));  // open: in3, gs, en_out, en_in
  and and_7 (ThreeAddress, Num[0], Num[1]);
  and and_8 (TwoAddress, ~Num[0], Num[1]);  // AND_Gate
  and and_9 (OneAddress, Num[0], ~Num[1]);  // AND_Gate
  and and_10 (ZeroAddress, ~Num[0], ~Num[1]);  // AND_Gate

  // Other names for the same wires on the sheet: RC[4:0] = Dest[4:0]; O2[7:0] = Input[7:0]; O1[7:0] = Input[15:8]
endmodule
