// Logisim project RISC 32 BIT MEMORY.circ as structural Verilog: 1 circuit, main circuit main
module main (
  input  [23:0] in_1,
  input  in_2,
  input  in_3,
  input  in_4,
  input  in_5,
  input  [23:0] in_6
);

  wire not_1_out;
  wire [31:0] IROUT, RAMOUT;

  not not_1 (not_1_out, in_2);
  RAM #(.addrWidth(24), .dataWidth(32)) ram_1 (
    .addr(in_1), .data(RAMOUT), .sel(in_2), .clk(in_3), .ld(in_4), .clr(in_5));
  ROM #(.addrWidth(24), .dataWidth(32)) rom_1 (.addr(in_6), .data(IROUT), .sel(not_1_out));

  // Other names for the same wires on the sheet: Address[23:0] = in_1; ClearRAM = in_5; Clock = in_3; CS = in_2;
  //   Load_Write = in_4; PC[23:0] = in_6
endmodule
