// Logisim project RISC 32 BIT REGISTERS.circ as structural Verilog: 1 circuit, main circuit main
module main (
  input  [31:0] in_1,
  input  [4:0] in_2,
  input  [4:0] in_3,
  input  [4:0] in_4,
  input  [4:0] in_5,
  input  in_6,
  input  in_7,
  input  in_8,
  input  in_9,
  input  in_10,
  output [31:0] out_11,
  output [31:0] out_12
);

  wire Clr0, Clr1, Clr2, Clr3, Clr4, Clr5, Clr6, Clr7, Clr8, Clr9, Clr10, Clr11, Clr12, Clr13, Clr14, Clr15,
       Clr16, Clr17, Clr18, Clr19, Clr20, Clr21, Clr22, Clr23, Clr24, Clr25, Clr26, Clr27, Clr28, Clr29,
       Clr30, Clr31, En0, En1, En2, En3, En4, En5, En6, En7, En8, En9, En10, En11, En12, En13, En14, En15,
       En16, En17, En18, En19, En20, En21, En22, En23, En24, En25, En26, En27, En28, En29, En30, En31;
  wire [31:0] multiplexer_1_out, multiplexer_2_out, Out14, OutR0, OutR1, OutR2, OutR3, OutR4, OutR5, OutR6,
       OutR7, OutR8, OutR9, OutR10, OutR11, OutR12, OutR13, OutR14, OutR15, OutR16, OutR17, OutR18, OutR19,
       OutR20, OutR21, OutR22, OutR23, OutR24, OutR25, OutR26, OutR27, OutR28, OutR29, OutR30, OutR31;

  Pull_Resistor pull_resistor_1 (.node(En0));
  Pull_Resistor pull_resistor_2 (.node(En1));
  Pull_Resistor pull_resistor_3 (.node(En2));
  Demultiplexer #(.select(5)) demultiplexer_1 (
    .out0(En0), .out1(En1), .out2(En2), .out3(En3), .out4(En4), .out5(En5), .out6(En6), .out7(En7),
    .out8(En8), .out9(En9), .out10(En10), .out11(En11), .out12(En12), .out13(En13), .out14(En14),
    .out15(En15), .out16(En16), .out17(En17), .out18(En18), .out19(En19), .out20(En20), .out21(En21),
    .out22(En22), .out23(En23), .out24(En24), .out25(En25), .out26(En26), .out27(En27), .out28(En28),
    .out29(En29), .out30(En30), .out31(En31), .in(1'b1), .sel(in_2), .en(in_7));
  Pull_Resistor pull_resistor_4 (.node(En4));
  Pull_Resistor pull_resistor_5 (.node(En5));
  Pull_Resistor pull_resistor_6 (.node(En9));
  Pull_Resistor pull_resistor_7 (.node(En3));
  Pull_Resistor pull_resistor_8 (.node(En10));
  Pull_Resistor pull_resistor_9 (.node(En6));
  Pull_Resistor pull_resistor_10 (.node(En8));
  Pull_Resistor pull_resistor_11 (.node(En7));
  Pull_Resistor pull_resistor_12 (.node(En11));
  Pull_Resistor pull_resistor_13 (.node(En17));
  Pull_Resistor pull_resistor_14 (.node(En18));
  Pull_Resistor pull_resistor_15 (.node(En13));
  Pull_Resistor pull_resistor_16 (.node(En16));
  Pull_Resistor pull_resistor_17 (.node(En12));
  Pull_Resistor pull_resistor_18 (.node(En15));
  Pull_Resistor pull_resistor_19 (.node(En14));
  Register #(.width(32)) R0 (.D(in_1), .en(En0), .Q(OutR0), .clk(in_6), .clr(Clr0));
  Register #(.width(32)) R8 (.D(in_1), .en(En8), .Q(OutR8), .clk(in_6), .clr(Clr8));
  Register #(.width(32)) R16 (.D(in_1), .en(En16), .Q(OutR16), .clk(in_6), .clr(Clr16));
  Register #(.width(32)) R24 (.D(in_1), .en(En24), .Q(OutR24), .clk(in_6), .clr(Clr24));
  Pull_Resistor pull_resistor_20 (.node(En26));
  Pull_Resistor pull_resistor_21 (.node(En19));
  Pull_Resistor pull_resistor_22 (.node(En20));
  Pull_Resistor pull_resistor_23 (.node(En22));
  Pull_Resistor pull_resistor_24 (.node(En23));
  Pull_Resistor pull_resistor_25 (.node(En25));
  Pull_Resistor pull_resistor_26 (.node(En21));
  Pull_Resistor pull_resistor_27 (.node(En24));
  Pull_Resistor pull_resistor_28 (.node(En28));
  Pull_Resistor pull_resistor_29 (.node(En30));
  Pull_Resistor pull_resistor_30 (.node(En29));
  Pull_Resistor pull_resistor_31 (.node(En31));
  Pull_Resistor pull_resistor_32 (.node(En27));
  Register #(.width(32)) R1 (.D(in_1), .en(En1), .Q(OutR1), .clk(in_6), .clr(Clr1));
  Register #(.width(32)) R9 (.D(in_1), .en(En9), .Q(OutR9), .clk(in_6), .clr(Clr9));
  Register #(.width(32)) R17 (.D(in_1), .en(En17), .Q(OutR17), .clk(in_6), .clr(Clr17));
  Register #(.width(32)) R25 (.D(in_1), .en(En25), .Q(OutR25), .clk(in_6), .clr(Clr25));
  Register #(.width(32)) R2 (.D(in_1), .en(En2), .Q(OutR2), .clk(in_6), .clr(Clr2));
  Register #(.width(32)) R10 (.D(in_1), .en(En10), .Q(OutR10), .clk(in_6), .clr(Clr10));
  Register #(.width(32)) R18 (.D(in_1), .en(En18), .Q(OutR18), .clk(in_6), .clr(Clr18));
  Register #(.width(32)) R26 (.D(in_1), .en(En26), .Q(OutR26), .clk(in_6), .clr(Clr26));
  Register #(.width(32)) R3 (.D(in_1), .en(En3), .Q(OutR3), .clk(in_6), .clr(Clr3));
  Register #(.width(32)) R11 (.D(in_1), .en(En11), .Q(OutR11), .clk(in_6), .clr(Clr11));
  Register #(.width(32)) R19 (.D(in_1), .en(En19), .Q(OutR19), .clk(in_6), .clr(Clr19));
  Register #(.width(32)) R27 (.D(in_1), .en(En27), .Q(OutR27), .clk(in_6), .clr(Clr27));
  Demultiplexer #(.select(5)) demultiplexer_2 (
    .out0(Clr0), .out1(Clr1), .out2(Clr2), .out3(Clr3), .out4(Clr4), .out5(Clr5), .out6(Clr6), .out7(Clr7),
    .out8(Clr8), .out9(Clr9), .out10(Clr10), .out11(Clr11), .out12(Clr12), .out13(Clr13), .out14(Clr14),
    .out15(Clr15), .out16(Clr16), .out17(Clr17), .out18(Clr18), .out19(Clr19), .out20(Clr20), .out21(Clr21),
    .out22(Clr22), .out23(Clr23), .out24(Clr24), .out25(Clr25), .out26(Clr26), .out27(Clr27), .out28(Clr28),
    .out29(Clr29), .out30(Clr30), .out31(Clr31), .in(1'b1), .sel(in_3), .en(in_8));
  Pull_Resistor pull_resistor_33 (.node(Clr4));
  Pull_Resistor pull_resistor_34 (.node(Clr1));
  Pull_Resistor pull_resistor_35 (.node(Clr5));
  Pull_Resistor pull_resistor_36 (.node(Clr0));
  Pull_Resistor pull_resistor_37 (.node(Clr6));
  Pull_Resistor pull_resistor_38 (.node(Clr3));
  Pull_Resistor pull_resistor_39 (.node(Clr2));
  Register #(.width(32)) R4 (.D(in_1), .en(En4), .Q(OutR4), .clk(in_6), .clr(Clr4));
  Register #(.width(32)) R12 (.D(in_1), .en(En12), .Q(OutR12), .clk(in_6), .clr(Clr12));
  Register #(.width(32)) R20 (.D(in_1), .en(En20), .Q(OutR20), .clk(in_6), .clr(Clr20));
  Register #(.width(32)) R28 (.D(in_1), .en(En28), .Q(OutR28), .clk(in_6), .clr(Clr28));
  Pull_Resistor pull_resistor_40 (.node(Clr10));
  Pull_Resistor pull_resistor_41 (.node(Clr14));
  Pull_Resistor pull_resistor_42 (.node(Clr13));
  Pull_Resistor pull_resistor_43 (.node(Clr8));
  Pull_Resistor pull_resistor_44 (.node(Clr12));
  Pull_Resistor pull_resistor_45 (.node(Clr7));
  Pull_Resistor pull_resistor_46 (.node(Clr11));
  Pull_Resistor pull_resistor_47 (.node(Clr9));
  Pull_Resistor pull_resistor_48 (.node(Clr22));
  Pull_Resistor pull_resistor_49 (.node(Clr19));
  Pull_Resistor pull_resistor_50 (.node(Clr18));
  Pull_Resistor pull_resistor_51 (.node(Clr21));
  Pull_Resistor pull_resistor_52 (.node(Clr16));
  Pull_Resistor pull_resistor_53 (.node(Clr20));
  Pull_Resistor pull_resistor_54 (.node(Clr17));
  Pull_Resistor pull_resistor_55 (.node(Clr15));
  Register #(.width(32)) R5 (.D(in_1), .en(En5), .Q(OutR5), .clk(in_6), .clr(Clr5));
  Register #(.width(32)) R13 (.D(in_1), .en(En13), .Q(OutR13), .clk(in_6), .clr(Clr13));
  Register #(.width(32)) R21 (.D(in_1), .en(En21), .Q(OutR21), .clk(in_6), .clr(Clr21));
  Register #(.width(32)) R29 (.D(in_1), .en(En29), .Q(OutR29), .clk(in_6), .clr(Clr29));
  Pull_Resistor pull_resistor_56 (.node(Clr24));
  Pull_Resistor pull_resistor_57 (.node(Clr26));
  Pull_Resistor pull_resistor_58 (.node(Clr28));
  Pull_Resistor pull_resistor_59 (.node(Clr29));
  Pull_Resistor pull_resistor_60 (.node(Clr23));
  Pull_Resistor pull_resistor_61 (.node(Clr27));
  Pull_Resistor pull_resistor_62 (.node(Clr25));
  Pull_Resistor pull_resistor_63 (.node(Clr30));
  Pull_Resistor pull_resistor_64 (.node(Clr31));
  Register #(.width(32)) R6 (.D(in_1), .en(En6), .Q(OutR6), .clk(in_6), .clr(Clr6));
  Register #(.width(32)) R14 (.D(in_1), .en(En14), .Q(Out14), .clk(in_6), .clr(Clr14));
  Register #(.width(32)) R22 (.D(in_1), .en(En22), .Q(OutR22), .clk(in_6), .clr(Clr22));
  Register #(.width(32)) R30 (.D(in_1), .en(En30), .Q(OutR30), .clk(in_6), .clr(Clr30));
  Register #(.width(32)) R7 (.D(in_1), .en(En7), .Q(OutR7), .clk(in_6), .clr(Clr7));
  Register #(.width(32)) R15 (.D(in_1), .en(En15), .Q(OutR15), .clk(in_6), .clr(Clr15));
  Register #(.width(32)) R23 (.D(in_1), .en(En23), .Q(OutR23), .clk(in_6), .clr(Clr23));
  Register #(.width(32)) R31 (.D(in_1), .en(En31), .Q(OutR31), .clk(in_6), .clr(Clr31));
  Multiplexer #(.select(5), .width(32)) multiplexer_1 (
    .in0(OutR0), .in1(OutR1), .in2(OutR2), .in3(OutR3), .in4(OutR4), .in5(OutR5), .in6(OutR6), .in7(OutR7),
    .in8(OutR8), .in9(OutR9), .in10(OutR10), .in11(OutR11), .in12(OutR12), .in13(OutR13), .in14(OutR14),
    .in15(OutR15), .in16(OutR16), .in17(OutR17), .in18(OutR18), .in19(OutR19), .in20(OutR20), .in21(OutR21),
    .in22(OutR22), .in23(OutR23), .in24(OutR24), .in25(OutR25), .in26(OutR26), .in27(OutR27), .in28(OutR28),
    .in29(OutR29), .in30(OutR30), .in31(OutR31), .out(multiplexer_1_out), .sel(in_4), .en(in_9));
  // Probe on multiplexer_1_out
  Register #(.width(32)) OP1 (.D(multiplexer_1_out), .en(1'b1), .Q(out_11), .clk(in_6), .clr(1'b0));
  Multiplexer #(.select(5), .width(32)) multiplexer_2 (
    .in0(OutR0), .in1(OutR1), .in2(OutR2), .in3(OutR3), .in4(OutR4), .in5(OutR5), .in6(OutR6), .in7(OutR7),
    .in8(OutR8), .in9(OutR9), .in10(OutR10), .in11(OutR11), .in12(OutR12), .in13(OutR13), .in14(OutR14),
    .in15(OutR15), .in16(OutR16), .in17(OutR17), .in18(OutR18), .in19(OutR19), .in20(OutR20), .in21(OutR21),
    .in22(OutR22), .in23(OutR23), .in24(OutR24), .in25(OutR25), .in26(OutR26), .in27(OutR27), .in28(OutR28),
    .in29(OutR29), .in30(OutR30), .in31(OutR31), .out(multiplexer_2_out), .sel(in_5), .en(in_10));
  // Probe on multiplexer_2_out
  Register #(.width(32)) OP2 (.D(multiplexer_2_out), .en(1'b1), .Q(out_12), .clk(in_6), .clr(1'b0));

  // Other names for the same wires on the sheet: Clock = in_6; CLR[4:0] = in_3; EnCLR = in_8; EnOP1 = in_9;
  //   EnOP2 = in_10; EnRC = in_7; Input[31:0] = in_1; OP1[31:0] = out_11; OP2[31:0] = out_12; REG1[4:0] = in_4;
  //   REG2[4:0] = in_5; SelectRC[4:0] = in_2
endmodule
